# Fritzing sketch jarvis (saved by Fritzing 0.9.6b)
breadboards: 1

parts:
  Raspberry_Pi_1 = Raspberry Pi 3 [part_number=RPI-3-V1.2]
  Part1 = Adafruit MAX98357A I2S 3W Class D Amplifier [part_number="Adafruit #3006"]
  LED1 = LED - 5mm [color="Red (633nm)" current=0.030 package="5 mm [THT]"]
  S1 = Toggle Switch [package=THT]

nets:
  N1: Raspberry_Pi_1.GPIO4, S1.L2
  N2: Raspberry_Pi_1.GPIO19, Part1.LRCLK
  N3: Raspberry_Pi_1.GPIO26, LED1.anode
  GND: Raspberry_Pi_1.GND, Part1.GND, LED1.cathode, S1.COM
  N4: Raspberry_Pi_1.GPIO21, Part1.DIN
  N5: Raspberry_Pi_1.GPIO18, Part1.BCLK
  5V: Raspberry_Pi_1.5V, Part1.VIN

custom parts:
  Adafruit MAX98357A I2S 3W Class D Amplifier: Listen to this good news - we now have an all in one digital audio amp breakout board that works incredibly well with the Raspberry Pi! If you're looking for an easy and low cost way to get you digital sound files bumpin' then the MAX08357 I2S Amp Breakout is for you. It takes standard I2S digital audio input and, not only decodes it into analog, but also amplifies it directly into a speaker.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
